// Logisim project ControlUnit.circ as structural Verilog: 9 circuits, main circuit Op_Code_Decoder
module Op_Code_Decoder (
  input  [5:0] OpCode,
  input  [5:0] FunCode,
  output addi,
  output beq,
  output slti,
  output add,
  output \and ,
  output nop,
  output andi,
  output bne,
  output sltiu,
  output sub,
  output \or ,
  output push,
  output ori,
  output blez,
  output lw,
  output pop,
  output mul,
  output \nor ,
  output xori,
  output bgtz,
  output sw,
  output tty,
  output mulu,
  output \xor ,
  output jmp,
  output bltz,
  output div,
  output mfhi,
  output halt,
  output mflo,
  output divu,
  output rnd,
  output slt,
  output jr,
  output kbd,
  output sltu
);

  wire and_18_out, and_19_out, and_20_out, and_21_out, and_22_out, and_23_out, and_24_out, and_25_out,
       and_34_out, and_35_out, and_36_out, and_37_out, and_38_out, and_39_out, and_40_out, and_48_out,
       and_49_out, and_50_out, and_51_out, and_52_out, and_53_out, and_54_out, special, stack, Tipo_R;

  and and_1 (addi, ~OpCode[0], ~OpCode[1], ~OpCode[2], OpCode[3], ~OpCode[4], ~OpCode[5]);  // AND_Gate
  and and_2 (andi, ~OpCode[0], ~OpCode[1], OpCode[2], OpCode[3], ~OpCode[4], ~OpCode[5]);  // AND_Gate
  and and_3 (ori, ~OpCode[0], ~OpCode[1], OpCode[2], OpCode[3], ~OpCode[4], ~OpCode[5]);  // AND_Gate
  and and_4 (xori, ~OpCode[0], ~OpCode[1], OpCode[2], OpCode[3], ~OpCode[4], ~OpCode[5]);  // AND_Gate
  and and_5 (jmp, ~OpCode[0], OpCode[1], ~OpCode[2], ~OpCode[3], ~OpCode[4], ~OpCode[5]);  // AND_Gate
  and and_6 (Tipo_R, ~OpCode[0], ~OpCode[1], ~OpCode[2], ~OpCode[3], ~OpCode[4], ~OpCode[5]);  // AND_Gate
  and and_7 (beq, ~OpCode[0], ~OpCode[1], OpCode[2], ~OpCode[3], ~OpCode[4], ~OpCode[5]);  // AND_Gate
  and and_8 (bne, OpCode[0], ~OpCode[1], OpCode[2], ~OpCode[3], ~OpCode[4], ~OpCode[5]);  // AND_Gate
  and and_9 (blez, ~OpCode[0], OpCode[1], OpCode[2], ~OpCode[3], ~OpCode[4], ~OpCode[5]);  // AND_Gate
  and and_10 (bgtz, OpCode[0], OpCode[1], OpCode[2], ~OpCode[3], ~OpCode[4], ~OpCode[5]);  // AND_Gate
  and and_11 (bltz, OpCode[0], ~OpCode[1], ~OpCode[2], ~OpCode[3], ~OpCode[4], ~OpCode[5]);  // AND_Gate
  and and_12 (stack, ~OpCode[0], ~OpCode[1], ~OpCode[2], OpCode[3], OpCode[4], OpCode[5]);  // AND_Gate
  and and_13 (slti, ~OpCode[0], OpCode[1], ~OpCode[2], OpCode[3], ~OpCode[4], ~OpCode[5]);  // AND_Gate
  and and_14 (sltiu, ~OpCode[0], OpCode[1], ~OpCode[2], OpCode[3], ~OpCode[4], ~OpCode[5]);  // AND_Gate
  and and_15 (lw, OpCode[0], OpCode[1], ~OpCode[2], ~OpCode[3], ~OpCode[4], OpCode[5]);  // AND_Gate
  and and_16 (sw, ~OpCode[0], ~OpCode[1], OpCode[2], ~OpCode[3], OpCode[4], ~OpCode[5]);  // AND_Gate
  and and_17 (special, OpCode[0], OpCode[1], OpCode[2], OpCode[3], OpCode[4], OpCode[5]);
  and and_18 (and_18_out, ~FunCode[0], ~FunCode[1], ~FunCode[2], ~FunCode[3], ~FunCode[4], FunCode[5]);  // AND_Gate
  and and_19 (and_19_out, ~FunCode[0], FunCode[1], ~FunCode[2], ~FunCode[3], ~FunCode[4], FunCode[5]);  // AND_Gate
  and and_20 (and_20_out, ~FunCode[0], ~FunCode[1], ~FunCode[2], FunCode[3], FunCode[4], ~FunCode[5]);  // AND_Gate
  and and_21 (and_21_out, FunCode[0], ~FunCode[1], ~FunCode[2], FunCode[3], FunCode[4], ~FunCode[5]);  // AND_Gate
  and and_22 (and_22_out, ~FunCode[0], FunCode[1], ~FunCode[2], FunCode[3], FunCode[4], ~FunCode[5]);  // AND_Gate
  and and_23 (and_23_out, FunCode[0], FunCode[1], ~FunCode[2], FunCode[3], FunCode[4], ~FunCode[5]);  // AND_Gate
  and and_24 (and_24_out, ~FunCode[0], FunCode[1], ~FunCode[2], FunCode[3], ~FunCode[4], FunCode[5]);  // AND_Gate
  and and_25 (and_25_out, FunCode[0], FunCode[1], ~FunCode[2], FunCode[3], ~FunCode[4], FunCode[5]);  // AND_Gate
  and and_26 (add, and_18_out, Tipo_R);
  and and_27 (sub, and_19_out, Tipo_R);
  and and_28 (mul, and_20_out, Tipo_R);
  and and_29 (mulu, and_21_out, Tipo_R);
  and and_30 (div, and_22_out, Tipo_R);
  and and_31 (divu, and_23_out, Tipo_R);
  and and_32 (slt, and_24_out, Tipo_R);
  and and_33 (sltu, and_25_out, Tipo_R);
  and and_34 (and_34_out, ~FunCode[0], ~FunCode[1], FunCode[2], ~FunCode[3], ~FunCode[4], FunCode[5]);  // AND_Gate
  and and_35 (and_35_out, FunCode[0], ~FunCode[1], FunCode[2], ~FunCode[3], ~FunCode[4], FunCode[5]);  // AND_Gate
  and and_36 (and_36_out, FunCode[0], FunCode[1], FunCode[2], ~FunCode[3], ~FunCode[4], FunCode[5]);  // AND_Gate
  and and_37 (and_37_out, ~FunCode[0], ~FunCode[1], ~FunCode[2], FunCode[3], ~FunCode[4], FunCode[5]);  // AND_Gate
  and and_38 (and_38_out, ~FunCode[0], ~FunCode[1], ~FunCode[2], ~FunCode[3], FunCode[4], ~FunCode[5]);  // AND_Gate
  and and_39 (and_39_out, ~FunCode[0], FunCode[1], ~FunCode[2], ~FunCode[3], FunCode[4], ~FunCode[5]);  // AND_Gate
  and and_40 (and_40_out, ~FunCode[0], ~FunCode[1], ~FunCode[2], FunCode[3], ~FunCode[4], ~FunCode[5]);  // AND_Gate
  and and_41 (\and , and_34_out, Tipo_R);
  and and_42 (\or , and_35_out, Tipo_R);
  and and_43 (\nor , and_36_out, Tipo_R);
  and and_44 (\xor , and_37_out, Tipo_R);
  and and_45 (mfhi, and_38_out, Tipo_R);
  and and_46 (mflo, and_39_out, Tipo_R);
  and and_47 (jr, and_40_out, Tipo_R);
  and and_48 (and_48_out, ~FunCode[0], ~FunCode[1], ~FunCode[2], ~FunCode[3], ~FunCode[4], ~FunCode[5]);  // AND_Gate
  and and_49 (and_49_out, FunCode[0], ~FunCode[1], ~FunCode[2], ~FunCode[3], ~FunCode[4], ~FunCode[5]);  // AND_Gate
  and and_50 (and_50_out, ~FunCode[0], ~FunCode[1], ~FunCode[2], ~FunCode[3], ~FunCode[4], ~FunCode[5]);  // AND_Gate
  and and_51 (and_51_out, FunCode[0], ~FunCode[1], ~FunCode[2], ~FunCode[3], ~FunCode[4], ~FunCode[5]);  // AND_Gate
  and and_52 (and_52_out, FunCode[0], FunCode[1], FunCode[2], FunCode[3], FunCode[4], FunCode[5]);
  and and_53 (and_53_out, ~FunCode[0], FunCode[1], ~FunCode[2], ~FunCode[3], ~FunCode[4], ~FunCode[5]);  // AND_Gate
  and and_54 (and_54_out, ~FunCode[0], ~FunCode[1], FunCode[2], ~FunCode[3], ~FunCode[4], ~FunCode[5]);  // AND_Gate
  and and_55 (nop, and_48_out, Tipo_R);
  and and_56 (push, and_49_out, stack);
  and and_57 (pop, and_50_out, stack);
  and and_58 (tty, and_51_out, special);
  and and_59 (halt, and_52_out, special);
  and and_60 (rnd, and_53_out, special);
  and and_61 (kbd, and_54_out, special);

  // Other names for the same wires on the sheet: f0 = FunCode[0]; f1 = FunCode[1]; f2 = FunCode[2]; f3 = FunCode[3];
  //   f4 = FunCode[4]; f5 = FunCode[5]; o0 = OpCode[0]; o1 = OpCode[1]; o2 = OpCode[2]; o3 = OpCode[3];
  //   o4 = OpCode[4]; o5 = OpCode[5]

  // Notes on the sheet:
  //   OP CODE
  //   GROUP
  //   FUNC CODE
endmodule

module Func_Code_Decoder (
  input  [5:0] FunCode,
  output add,
  output \and ,
  output nop_pop,
  output sub,
  output \or ,
  output push_tty,
  output mul,
  output \nor ,
  output halt,
  output mulu,
  output \xor ,
  output rnd,
  output kbd,
  output div,
  output mfhi,
  output mflo,
  output divu,
  output slt,
  output jr,
  output sltu
);

  and and_1 (add, ~FunCode[0], ~FunCode[1], ~FunCode[2], ~FunCode[3], ~FunCode[4], FunCode[5]);  // AND_Gate
  and and_2 (sub, ~FunCode[0], FunCode[1], ~FunCode[2], ~FunCode[3], ~FunCode[4], FunCode[5]);  // AND_Gate
  and and_3 (mul, ~FunCode[0], ~FunCode[1], ~FunCode[2], FunCode[3], FunCode[4], ~FunCode[5]);  // AND_Gate
  and and_4 (mulu, FunCode[0], ~FunCode[1], ~FunCode[2], FunCode[3], FunCode[4], ~FunCode[5]);  // AND_Gate
  and and_5 (div, ~FunCode[0], FunCode[1], ~FunCode[2], FunCode[3], FunCode[4], ~FunCode[5]);  // AND_Gate
  and and_6 (divu, FunCode[0], FunCode[1], ~FunCode[2], FunCode[3], FunCode[4], ~FunCode[5]);  // AND_Gate
  and and_7 (slt, ~FunCode[0], FunCode[1], ~FunCode[2], FunCode[3], ~FunCode[4], FunCode[5]);  // AND_Gate
  and and_8 (sltu, FunCode[0], FunCode[1], ~FunCode[2], FunCode[3], ~FunCode[4], FunCode[5]);  // AND_Gate
  and and_9 (\and , ~FunCode[0], ~FunCode[1], FunCode[2], ~FunCode[3], ~FunCode[4], FunCode[5]);  // AND_Gate
  and and_10 (\or , FunCode[0], ~FunCode[1], FunCode[2], ~FunCode[3], ~FunCode[4], FunCode[5]);  // AND_Gate
  and and_11 (\nor , FunCode[0], FunCode[1], FunCode[2], ~FunCode[3], ~FunCode[4], FunCode[5]);  // AND_Gate
  and and_12 (\xor , ~FunCode[0], ~FunCode[1], ~FunCode[2], FunCode[3], ~FunCode[4], FunCode[5]);  // AND_Gate
  and and_13 (mfhi, ~FunCode[0], ~FunCode[1], ~FunCode[2], ~FunCode[3], FunCode[4], ~FunCode[5]);  // AND_Gate
  and and_14 (mflo, ~FunCode[0], FunCode[1], ~FunCode[2], ~FunCode[3], FunCode[4], ~FunCode[5]);  // AND_Gate
  and and_15 (jr, ~FunCode[0], ~FunCode[1], ~FunCode[2], FunCode[3], ~FunCode[4], ~FunCode[5]);  // AND_Gate
  and and_16 (nop_pop, ~FunCode[0], ~FunCode[1], ~FunCode[2], ~FunCode[3], ~FunCode[4], ~FunCode[5]);  // AND_Gate
  and and_17 (push_tty, FunCode[0], ~FunCode[1], ~FunCode[2], ~FunCode[3], ~FunCode[4], ~FunCode[5]);  // AND_Gate
  and and_18 (halt, FunCode[0], FunCode[1], FunCode[2], FunCode[3], FunCode[4], FunCode[5]);
  and and_19 (rnd, ~FunCode[0], FunCode[1], ~FunCode[2], ~FunCode[3], ~FunCode[4], ~FunCode[5]);  // AND_Gate
  and and_20 (kbd, ~FunCode[0], ~FunCode[1], FunCode[2], ~FunCode[3], ~FunCode[4], ~FunCode[5]);  // AND_Gate

  // Other names for the same wires on the sheet: f0 = FunCode[0]; f1 = FunCode[1]; f2 = FunCode[2]; f3 = FunCode[3];
  //   f4 = FunCode[4]; f5 = FunCode[5]
endmodule

module ControlUnit (
  input  [5:0] in_1,
  input  [5:0] in_2,
  input  in_3,
  input  in_4,
  input  in_5,
  output out_6,
  output [2:0] out_7,
  output out_8,
  output [2:0] out_9,
  output out_10,
  output [1:0] out_11,
  output out_12,
  output out_13,
  output out_14,
  output [1:0] out_15,
  output out_16,
  output out_17,
  output out_18,
  output [2:0] out_19,
  output out_20,
  output [1:0] out_21,
  output out_22,
  output out_23,
  output out_24
);

  wire add, addi, \and , andi, beq, bgtz, blez, bltz, bne, d_ff_1_q, d_ff_2_q, d_ff_3_q,
       demultiplexer_1_out0, demultiplexer_1_out1, demultiplexer_2_out0, div, divu, En_AL, En_B, En_I, En_S,
       En_Sp, En_W, EndS, Endw, haltl, haltl_En, jmp, jr, kbd_t, Load_IM_q, lw, mfhi, mflo, mult, mulu, next,
       nop_pop, \nor , not_1_out, \or , or_2_out, or_3_out, or_6_out, or_7_out, or_9_out, ori, PCal, PCb,
       PCi, PCs, PCsp, PCw, pop, push, push_tty, RamWs, RamWw, RFal, RfE, RFi, Rfs, Rfw, rnd, S_DAi, S_DAw,
       slt, slti, sltiu, sltu, special, stack, StartRamF, StartRams, StartRamw, sub, sw, TipoAl, Type_B,
       Type_I, Type_S, Type_Sp, Type_W, \xor , xori;
  wire [1:0] S_Adrs, S_Adrw, S_BCal, S_Bi, S_Bs, S_Bw;
  wire [2:0] S_ALUal, S_ALUb, S_ALUi, S_ALUs, S_Dial, S_DiE, S_Dis, S_Diw;

  Func_Code_Decoder func_code_decoder_1 (
    .add(add), .\and (\and ), .nop_pop(nop_pop), .sub(sub), .\or (\or ), .push_tty(push_tty), .mul(mult),
    .\nor (\nor ), .halt(haltl), .mulu(mulu), .\xor (\xor ), .rnd(rnd), .kbd(kbd_t), .div(div), .mfhi(mfhi),
    .mflo(mflo), .divu(divu), .slt(slt), .jr(jr), .sltu(sltu), .FunCode(in_2));
  Op_Code_Decoder op_code_decoder_1 ();  // open: beq, addi, bne, andi, blez, ori, bgtz, xori, lw, slti, sw, sltiu, bltz, OpCode, jmp, add, and, nop, FunCode, sub, or, push, mul, nor, halt, mulu, xor, rnd, kbd, div, mfhi, mflo, divu, slt, jr, sltu, pop, tty
  Demultiplexer #(.enable("false")) demultiplexer_1 (
    .out0(demultiplexer_1_out0), .out1(demultiplexer_1_out1), .in(d_ff_1_q), .sel(not_1_out));
  D_Flip_Flop d_ff_1 (.clk(in_3), .D(demultiplexer_1_out0), .Q(d_ff_1_q), .preset(in_4));  // open: Qn, en, reset
  not not_1 (not_1_out, in_4);
  or or_1 (StartRamF, next, demultiplexer_1_out1);
  D_Flip_Flop d_ff_2 (.clk(in_3), .D(demultiplexer_2_out0), .Q(d_ff_2_q));  // open: Qn, preset, en, reset
  or or_2 (or_2_out, StartRamF, d_ff_2_q);
  Demultiplexer #(.enable("false")) demultiplexer_2 (
    .out0(demultiplexer_2_out0), .out1(out_12), .in(or_2_out), .sel(in_5));
  Type_AL type_al_1 (
    .in_1(En_AL), .in_2(add), .in_3(sub), .in_4(\and ), .in_5(\or ), .in_6(\xor ), .in_7(\nor ), .in_8(slt),
    .in_9(sltu), .in_10(mult), .in_11(mulu), .in_16(jr), .in_12(div), .in_13(divu), .in_14(mfhi),
    .in_15(mflo), .out_19(RFal), .out_20(S_ALUal), .out_22(S_Dial), .out_23(S_BCal), .out_18(PCal),
    .in_17(nop_pop), .out_21(out_6));
  D_Flip_Flop Load_IM (.clk(in_3), .D(out_12), .Q(Load_IM_q));  // open: Qn, preset, en, reset
  and and_1 (En_AL, TipoAl, Load_IM_q);
  and and_2 (En_I, Type_I, Load_IM_q);
  and and_3 (En_B, Type_B, Load_IM_q);
  and and_4 (En_W, Type_W, Load_IM_q);
  and and_5 (En_Sp, Type_Sp, Load_IM_q);
  and and_6 (En_S, Type_S, Load_IM_q);
  TypeWord typeword_1 (
    .in_2(in_3), .in_3(lw), .in_4(in_5), .in_5(sw), .out_6(Rfw), .out_7(S_DAw), .out_8(Endw), .in_1(En_W),
    .out_10(S_Bw), .out_12(S_Adrw), .out_14(PCw), .out_11(RamWw), .out_13(S_Diw), .out_9(StartRamw));
  Type_Stack type_stack_1 (
    .in_1(pop), .in_2(push), .in_3(En_S), .in_4(in_5), .in_5(in_3), .out_13(EndS), .out_10(StartRams),
    .out_12(PCs), .out_9(S_Adrs), .out_11(out_13), .out_17(out_18), .out_8(out_16), .out_7(RamWs),
    .out_6(Rfs), .out_16(S_ALUs), .out_15(S_Dis), .out_14(S_Bs));
  or or_3 (or_3_out, En_AL, En_I, En_Sp, En_B);
  D_Flip_Flop d_ff_3 (.clk(in_3), .D(or_3_out), .Q(d_ff_3_q));  // open: Qn, preset, en, reset
  Type_Inmediate type_inmediate_1 (
    .in_1(En_I), .in_2(addi), .in_3(andi), .in_4(ori), .in_5(xori), .in_6(slti), .in_7(sltiu),
    .out_10(S_DAi), .out_9(S_Bi), .out_8(S_ALUi), .out_11(PCi), .out_12(RFi));
  or or_4 (next, d_ff_3_q, Endw, EndS);
  Type_Branch type_branch_1 (
    .in_1(En_B), .in_2(beq), .in_3(bne), .in_4(blez), .in_5(bgtz), .in_6(bltz), .out_8(PCb), .out_9(S_ALUb),
    .out_11(out_19), .out_10(out_21), .in_7(jmp));
  or or_5 (Type_B, beq, bne, blez, bgtz, bltz, jmp);
  and and_7 (Type_Sp, special, or_6_out);
  or or_6 (or_6_out, kbd_t, rnd, push_tty);
  and and_8 (pop, push_tty, stack);
  and and_9 (push, stack, nop_pop);
  or or_7 (or_7_out, haltl_En, out_24);
  or or_8 (Type_W, lw, sw);
  or or_9 (or_9_out, pop, push);
  D_Flip_Flop #(.trigger("high")) Halt (.clk(in_3), .D(or_7_out), .Q(out_24));  // open: Qn, preset, en, reset
  or or_10 (Type_I, addi, andi, ori, xori, slti, sltiu);
  and and_10 (Type_S, stack, or_9_out);
  and and_11 (haltl_En, special, haltl);
  Type_Specials type_specials_1 (
    .in_2(kbd_t), .in_3(rnd), .in_4(special), .in_5(push_tty), .out_9(out_17), .out_7(S_DiE), .in_1(En_Sp),
    .out_6(RfE), .out_8(out_23), .out_10(PCsp));
  assign out_7 = S_ALUal | S_ALUi | S_ALUb | S_ALUs;  // OR_Gate or_11, 3 bits wide
  assign out_15 = S_BCal | S_Bs | S_Bi | out_21 | S_Bw;  // OR_Gate or_12, 2 bits wide
  assign out_9 = S_Dial | S_Dis | S_Diw | S_DiE;  // OR_Gate or_13, 3 bits wide
  assign out_11 = S_Adrs | S_Adrw;  // OR_Gate or_14, 2 bits wide
  or or_15 (out_22, S_DAi, S_DAw);
  or or_16 (out_10, RamWs, RamWw);
  or or_17 (out_20, StartRams, StartRamF, StartRamw);
  or or_18 (out_8, RfE, RFal, RFi, Rfw);
  or or_19 (out_14, PCal, PCi, PCsp, PCb, PCw);

  // Other names for the same wires on the sheet: Clk = in_3; FunCode[5:0] = in_2; HALT = out_24; En_KBD = out_23;
  //   KBD = out_23; L_IM = out_12; L_LoHi = out_6; LH = out_6; OpCode[5:0] = in_1; PC = out_14; RamReady = in_5;
  //   RamW = out_10; Rf_Rw = out_8; S_Adr[1:0] = out_11; S_ALU[2:0] = out_7; S_A = out_13; S_As = out_13;
  //   S_B[1:0] = out_15; S_BC[1:0] = out_21; S_BCb[1:0] = out_21; S_DA = out_22; S_Di[2:0] = out_9; S_DO = out_16;
  //   S_flag[2:0] = out_19; S_flags[2:0] = out_19; SP = out_18; SPs = out_18; start = in_4; StartRam = out_20;
  //   TTY = out_17; tty_En = out_17; Type_AL = TipoAl

  // Notes on the sheet:
  //   Inputs
  //   Decoders
  //   IDLE
  //   General Circuit
  //   FETCH
  //   SWITCH
  //   Group Circuits
  //   End/Next
  //   Groups
  //   Selectors
  //   Loads
endmodule

module Type_AL (
  input  in_1,
  input  in_2,
  input  in_3,
  input  in_4,
  input  in_5,
  input  in_6,
  input  in_7,
  input  in_8,
  input  in_9,
  input  in_10,
  input  in_11,
  input  in_12,
  input  in_13,
  input  in_14,
  input  in_15,
  input  in_16,
  input  in_17,
  output out_18,
  output out_19,
  output [2:0] out_20,
  output out_21,
  output [2:0] out_22,
  output [1:0] out_23
);

  wire and_3_out, not_1_out, or_1_out, or_6_out, or_7_out, or_8_out;

  or or_1 (or_1_out, in_10, in_11, in_12, in_13);
  not not_1 (not_1_out, in_14);
  or or_2 (out_22[0], in_15, in_14);
  or or_3 (out_20[0], in_7, in_3, in_5, in_11, in_9, in_13);
  or or_4 (out_20[1], in_13, in_4, in_5, in_8, in_9, in_12);
  or or_5 (out_20[2], in_6, in_8, in_7, in_9);
  and and_1 (out_21, or_1_out, in_1);
  and and_2 (out_22[1], in_15, not_1_out);
  or or_6 (or_6_out, out_20[0], out_20[1], out_20[2]);
  or or_7 (or_7_out, in_2, or_6_out);
  or or_8 (or_8_out, or_7_out, in_14, in_15);
  and and_3 (and_3_out, or_8_out, ~in_11, ~in_12, ~in_13);  // AND_Gate
  and and_4 (out_19, and_3_out, in_1);

  assign out_18 = in_1;
  assign out_22[2] = in_14;
  assign out_23 = {in_16, 1'b0};

  // Other names for the same wires on the sheet: add = in_2; and = in_4; div = in_12; divu = in_13; LH = out_21;
  //   mflo = in_15; mult = in_10; mulu = in_11; nop = in_17; nor = in_7; or = in_5; EN = in_1; PC = in_1;
  //   Rf_Rw = out_19; S_ALU[2:0] = out_20; jr = in_16; S_BC[1] = in_16; S_Di[2:0] = {in_14, out_22[1:0]};
  //   mfhi = in_14; slt = in_8; sltu = in_9; sub = in_3; xor = in_6
endmodule

module Type_Inmediate (
  input  in_1,
  input  in_2,
  input  in_3,
  input  in_4,
  input  in_5,
  input  in_6,
  input  in_7,
  output [2:0] out_8,
  output [1:0] out_9,
  output out_10,
  output out_11,
  output out_12
);

  wire or_3_out;

  or or_1 (out_9[0], in_2, in_3, in_4, in_5, in_6, in_7);
  or or_2 (out_8[0], in_4, in_7);
  or or_3 (or_3_out, in_6, in_3);
  or or_4 (out_8[2], in_7, in_6, in_5);
  or or_5 (out_8[1], out_8[0], or_3_out);

  assign out_9[1] = 1'b0;
  assign out_10 = out_9[0];
  assign out_11 = in_1;
  assign out_12 = in_1;

  // Other names for the same wires on the sheet: addi = in_2; andi = in_3; ori = in_4; Enable = in_1; PC = in_1;
  //   RW_RF = in_1; S_ALU[2:0] = out_8; S_B[0] = out_9[0]; S_DA = out_9[0]; slti = in_6; sltiu = in_7; xori = in_5
endmodule

module Type_Branch (
  input  in_1,
  input  in_2,
  input  in_3,
  input  in_4,
  input  in_5,
  input  in_6,
  input  in_7,
  output out_8,
  output [2:0] out_9,
  output [1:0] out_10,
  output [2:0] out_11
);

  wire or_4_out;

  or or_1 (out_9[0], in_2, in_3, in_4, in_5, in_6);
  or or_2 (out_11[2], in_6, in_5);
  nor nor_1 (out_11[1], in_2, in_4);
  or or_3 (out_11[0], in_4, in_5);
  or or_4 (or_4_out, out_9[0], in_7);
  and and_1 (out_10[0], or_4_out, in_1);
  and and_2 (out_10[1], in_1, in_7);

  assign out_8 = in_1;
  assign out_9[2:1] = 2'b00;

  // Other names for the same wires on the sheet: beq = in_2; bgtz = in_5; blez = in_4; bltz = in_6; bne = in_3;
  //   jmp = in_7; Enable = in_1; PC = in_1; S_ALU[0] = out_9[0]; S_BC[1:0] = out_10; S_flags[2:0] = out_11
endmodule

module TypeWord (
  input  in_1,
  input  in_2,
  input  in_3,
  input  in_4,
  input  in_5,
  output out_6,
  output out_7,
  output out_8,
  output out_9,
  output [1:0] out_10,
  output out_11,
  output [1:0] out_12,
  output [2:0] out_13,
  output out_14
);

  wire and_1_out, and_2_out, d_ff_1_q, d_ff_2_q, demultiplexer_1_out0, demultiplexer_2_out0, EndLW, EndSW,
       PCs, S_Adr0l;

  and and_1 (and_1_out, in_1, in_3);
  D_Flip_Flop d_ff_1 (.clk(in_2), .D(demultiplexer_1_out0), .Q(d_ff_1_q));  // open: Qn, preset, en, reset
  and and_2 (and_2_out, in_1, in_5);
  D_Flip_Flop d_ff_2 (.clk(in_2), .D(demultiplexer_2_out0), .Q(d_ff_2_q));  // open: Qn, preset, en, reset
  or or_1 (S_Adr0l, and_1_out, d_ff_1_q);
  or or_2 (out_11, and_2_out, d_ff_2_q);
  Demultiplexer #(.enable("false")) demultiplexer_1 (
    .out0(demultiplexer_1_out0), .out1(out_6), .in(S_Adr0l), .sel(in_4));
  Demultiplexer #(.enable("false")) demultiplexer_2 (.out0(demultiplexer_2_out0), .out1(PCs), .in(out_11), .sel(in_4));
  D_Flip_Flop d_ff_3 (.clk(in_2), .D(PCs), .Q(EndSW));  // open: Qn, preset, en, reset
  D_Flip_Flop d_ff_4 (.clk(in_2), .D(out_6), .Q(EndLW));  // open: Qn, preset, en, reset
  or or_3 (out_8, EndLW, EndSW);
  or or_4 (out_9, S_Adr0l, out_11);
  or or_5 (out_10[0], out_11, S_Adr0l);
  or or_6 (out_12[0], S_Adr0l, out_11);
  or or_7 (out_14, out_6, PCs);

  assign out_7 = out_6;
  assign out_10[1] = 1'b0;
  assign out_12[1] = 1'b0;
  assign out_13 = {2'b00, out_6};

  // Other names for the same wires on the sheet: Clk = in_2; EN = in_1; ENDw = out_8; LoadWord = in_3; PC = out_14;
  //   RamReady = in_4; S_Adr[0] = out_12[0]; S_B[0] = out_10[0]; PCl = out_6; Rf_Rw = out_6; S_DA = out_6;
  //   S_Di[0] = out_6; S_Di0 = out_6; startRam = out_9; S_B0l = S_Adr0l; startRaml = S_Adr0l; RamW = out_11;
  //   S_Adr0s = out_11; S_B0s = out_11; startRams = out_11; StoreWord = in_5

  // Notes on the sheet:
  //   LOAD
  //   STORE
endmodule

module Type_Specials (
  input  in_1,
  input  in_2,
  input  in_3,
  input  in_4,
  input  in_5,
  output out_6,
  output [2:0] out_7,
  output out_8,
  output out_9,
  output out_10
);

  and and_1 (out_9, in_4, in_1, in_5);

  assign out_6 = in_2;
  assign out_7 = {3{in_2}};
  assign out_8 = in_2;
  assign out_10 = in_1;

  // Other names for the same wires on the sheet: En = in_1; PC = in_1; push_tty = in_5; rnd = in_3; kbd = in_2;
  //   kbdEn = in_2; Rf = in_2; S_Di[2:0] = {3{in_2}}; special = in_4; tty_Enable = out_9
endmodule

module Type_Stack (
  input  in_1,
  input  in_2,
  input  in_3,
  input  in_4,
  input  in_5,
  output out_6,
  output out_7,
  output out_8,
  output [1:0] out_9,
  output out_10,
  output out_11,
  output out_12,
  output out_13,
  output [1:0] out_14,
  output [2:0] out_15,
  output [2:0] out_16,
  output out_17
);

  wire and_1_out, d_ff_1_q, d_ff_2_q, d_ff_3_q, demultiplexer_1_out0, demultiplexer_2_out0, EndPop, EndPush,
       PCpush, S_Adr1pop;

  or or_1 (out_11, out_6, out_16[0]);
  or or_2 (out_14[1], out_6, out_16[0]);
  and and_1 (and_1_out, in_3, in_1);
  D_Flip_Flop d_ff_1 (.clk(in_5), .D(demultiplexer_1_out0), .Q(d_ff_1_q));  // open: Qn, preset, en, reset
  and and_2 (out_16[0], in_3, in_2);
  or or_3 (S_Adr1pop, and_1_out, d_ff_1_q);
  or or_4 (out_9[0], S_Adr1pop, out_7);
  or or_5 (out_17, out_6, out_16[0]);
  Demultiplexer #(.enable("false")) demultiplexer_1 (
    .out0(demultiplexer_1_out0), .out1(out_6), .in(S_Adr1pop), .sel(in_4));
  D_Flip_Flop d_ff_2 (.clk(in_5), .D(out_16[0]), .Q(d_ff_2_q));  // open: Qn, preset, en, reset
  D_Flip_Flop d_ff_3 (.clk(in_5), .D(demultiplexer_2_out0), .Q(d_ff_3_q));  // open: Qn, preset, en, reset
  or or_6 (out_12, out_6, PCpush);
  or or_7 (out_7, d_ff_2_q, d_ff_3_q);
  or or_8 (out_10, S_Adr1pop, out_7);
  D_Flip_Flop d_ff_4 (.clk(in_5), .D(out_6), .Q(EndPop));  // open: Qn, preset, en, reset
  Demultiplexer #(.enable("false")) demultiplexer_2 (
    .out0(demultiplexer_2_out0), .out1(PCpush), .in(out_7), .sel(in_4));
  or or_9 (out_13, EndPop, EndPush);
  D_Flip_Flop d_ff_5 (.clk(in_5), .D(PCpush), .Q(EndPush));  // open: Qn, preset, en, reset

  assign out_8 = out_7;
  assign out_9[1] = 1'b0;
  assign out_14[0] = out_14[1];
  assign out_15 = {2'b00, out_6};
  assign out_16[2:1] = 2'b00;

  // Other names for the same wires on the sheet: Clk = in_5; En = in_3; ENDStack = out_13; PC = out_12; pop = in_1;
  //   push = in_2; RamReady = in_4; S_A = out_11; S_Adr[0] = out_9[0]; S_ALU[0] = out_16[0]; S_ALU0 = out_16[0];
  //   S_Apush = out_16[0]; S_Bpush = out_16[0]; SP_RWpush = out_16[0]; S_B[1:0] = {2{out_14[1]}}; PCpop = out_6;
  //   Rf_Rw = out_6; S_Apop = out_6; S_Bpop = out_6; S_Di[0] = out_6; S_Di0 = out_6; SP_RWpop = out_6; SP_RW = out_17;
  //   startRam = out_10; startRampop = S_Adr1pop; RamW = out_7; S_Adr1push = out_7; S_Do = out_7;
  //   startRampush = out_7

  // Notes on the sheet:
  //   POP
  //   PUSH
endmodule
