// Logisim project DataPath.circ as structural Verilog
module Register_File_32x32_bits (
  input  [4:0] DA,
  input  [31:0] DI,
  input  R_W,
  input  [4:0] SA,
  input  [4:0] SB,
  input  Clk,
  input  Reset,
  input  [31:0] Lo,
  input  [31:0] Hi,
  input  LH_RW,
  input  [31:0] SP,
  input  LH_RW_2,
  output [31:0] Data_A,
  output [31:0] Stack_Pointer,
  output [31:0] Data_B,
  output [31:0] Lo_2,
  output [31:0] Hi_2
);

  wire and_1_out, and_2_out, and_3_out, and_4_out, and_5_out, L0, L1, L2, L3, L4, L5, L6, L7, L8, L9, L10,
       L11, L12, L13, L14, L15, L16, L17, L18, L19, L20, L21, L22, L23, L24, L25, L26, L27, L28, L29, L30,
       L31;
  wire [31:0] R0, R1, R2, R3, R4, R5, R6, R7, R8, R9, R10, R11, R12, R13, R14, R15, R16, R17, R18, R19, R20,
       R21, R22, R23, R24, R25, R26, R27, R28, R29, R30, SPIn;

  Decoder #(.select(5), .enable("false")) decoder_1 (
    .out0(L0), .out1(L1), .out2(L2), .out3(L3), .out4(L4), .out5(L5), .out6(L6), .out7(L7), .out8(L8),
    .out9(L9), .out10(L10), .out11(L11), .out12(L12), .out13(L13), .out14(L14), .out15(L15), .out16(L16),
    .out17(L17), .out18(L18), .out19(L19), .out20(L20), .out21(L21), .out22(L22), .out23(L23), .out24(L24),
    .out25(L25), .out26(L26), .out27(L27), .out28(L28), .out29(L29), .out30(L30), .out31(L31), .sel(DA));
  Register_32_bits register_32_bits_1 (.Data_In(Lo), .Clock(Clk), .Reset(Reset), .Current_Value(Lo_2), .Load(LH_RW));
  Register_32_bits register_32_bits_2 (.Data_In(Hi), .Clock(Clk), .Reset(Reset), .Current_Value(Hi_2), .Load(LH_RW));
  and and_1 (and_1_out, L0, R_W);
  and and_2 (and_2_out, L1, R_W);
  and and_3 (and_3_out, L2, R_W);
  and and_4 (and_4_out, L3, R_W);
  and and_5 (and_5_out, L4, R_W);
  Register #(.width(32)) register_1 (.D(DI), .en(and_1_out), .Q(R0), .clk(Clk), .clr(Reset));
  Register #(.width(32)) register_2 (.D(DI), .en(and_2_out), .Q(R1), .clk(Clk), .clr(Reset));
  Register #(.width(32), .trigger("falling")) register_3 (.D(DI), .en(and_3_out), .Q(R2), .clk(Clk), .clr(Reset));
  Register #(.width(32)) register_4 (.D(DI), .en(and_4_out), .Q(R3), .clk(Clk), .clr(Reset));
  Register #(.width(32), .trigger("falling")) register_5 (.D(DI), .en(and_5_out), .Q(R4), .clk(Clk), .clr(Reset));
  Register_32_bits register_32_bits_3 (.Data_In(DI), .Clock(Clk), .Reset(Reset), .Current_Value(R5), .Load(L5));
  Register_32_bits register_32_bits_4 (.Data_In(DI), .Clock(Clk), .Reset(Reset), .Current_Value(R6), .Load(L6));
  Register_32_bits register_32_bits_5 (.Data_In(DI), .Clock(Clk), .Reset(Reset), .Current_Value(R7), .Load(L7));
  Register_32_bits register_32_bits_6 (.Data_In(DI), .Clock(Clk), .Reset(Reset), .Current_Value(R8), .Load(L8));
  Register_32_bits register_32_bits_7 (.Data_In(DI), .Clock(Clk), .Reset(Reset), .Current_Value(R9), .Load(L9));
  Register_32_bits register_32_bits_8 (.Data_In(DI), .Clock(Clk), .Reset(Reset), .Current_Value(R10), .Load(L10));
  Register_32_bits register_32_bits_9 (.Data_In(DI), .Clock(Clk), .Reset(Reset), .Current_Value(R11), .Load(L11));
  Register_32_bits register_32_bits_10 (.Data_In(DI), .Clock(Clk), .Reset(Reset), .Current_Value(R12), .Load(L12));
  Register_32_bits register_32_bits_11 (.Data_In(DI), .Clock(Clk), .Reset(Reset), .Current_Value(R13), .Load(L13));
  Register_32_bits register_32_bits_12 (.Data_In(DI), .Clock(Clk), .Reset(Reset), .Current_Value(R14), .Load(L14));
  Register_32_bits register_32_bits_13 (.Data_In(DI), .Clock(Clk), .Reset(Reset), .Current_Value(R15), .Load(L15));
  Register_32_bits register_32_bits_14 (.Data_In(DI), .Clock(Clk), .Reset(Reset), .Current_Value(R16), .Load(L16));
  Register_32_bits register_32_bits_15 (.Data_In(DI), .Clock(Clk), .Reset(Reset), .Current_Value(R17), .Load(L17));
  Register_32_bits register_32_bits_16 (.Data_In(DI), .Clock(Clk), .Reset(Reset), .Current_Value(R18), .Load(L18));
  Register_32_bits register_32_bits_17 (.Data_In(DI), .Clock(Clk), .Reset(Reset), .Current_Value(R19), .Load(L19));
  Register_32_bits register_32_bits_18 (.Data_In(DI), .Clock(Clk), .Reset(Reset), .Current_Value(R20), .Load(L20));
  Register_32_bits register_32_bits_19 (.Data_In(DI), .Clock(Clk), .Reset(Reset), .Current_Value(R21), .Load(L21));
  Register_32_bits register_32_bits_20 (.Data_In(DI), .Clock(Clk), .Reset(Reset), .Current_Value(R22), .Load(L22));
  Register_32_bits register_32_bits_21 (.Data_In(DI), .Clock(Clk), .Reset(Reset), .Current_Value(R23), .Load(L23));
  // Register_32_bits register_32_bits_22: pin names not known; wires that end beside it: DI, L24, Clk, Reset, R24
  // Register_32_bits register_32_bits_23: pin names not known; wires that end beside it: DI, L25, Clk, Reset, R25
  // Register_32_bits register_32_bits_24: pin names not known; wires that end beside it: DI, L26, Clk, Reset, R26
  // Register_32_bits register_32_bits_25: pin names not known; wires that end beside it: DI, L27, Clk, Reset, R27
  // Register_32_bits register_32_bits_26: pin names not known; wires that end beside it: DI, L28, Clk, Reset, R28
  // Register_32_bits register_32_bits_27: pin names not known; wires that end beside it: DI, L29, Clk, Reset, R29
  // Register_32_bits register_32_bits_28: pin names not known; wires that end beside it: DI, L30, Clk, Reset, R30
  Register_32_bits register_32_bits_29 (
    .Data_In(SPIn), .Clock(Clk), .Reset(Reset), .Current_Value(Stack_Pointer), .Load(L31));
  Multiplexer #(.select(5), .width(32), .enable("false")) multiplexer_1 (
    .in0(R0), .in1(R1), .in2(R2), .in3(R3), .in4(R4), .in5(R5), .in6(R6), .in7(R7), .in8(R8), .in9(R9),
    .in10(R10), .in11(R11), .in12(R12), .in13(R13), .in14(R14), .in15(R15), .in16(R16), .in17(R17),
    .in18(R18), .in19(R19), .in20(R20), .in21(R21), .in22(R22), .in23(R23), .in24(R24), .in25(R25),
    .in26(R26), .in27(R27), .in28(R28), .in29(R29), .in30(R30), .out(Data_A), .sel(SA));  // open: in31
  Multiplexer #(.select(5), .width(32), .enable("false")) multiplexer_2 (
    .in0(R0), .in1(R1), .in2(R2), .in3(R3), .in4(R4), .in5(R5), .in6(R6), .in7(R7), .in8(R8), .in9(R9),
    .in10(R10), .in11(R11), .in12(R12), .in13(R13), .in14(R14), .in15(R15), .in16(R16), .in17(R17),
    .in18(R18), .in19(R19), .in20(R20), .in21(R21), .in22(R22), .in23(R23), .in24(R24), .in25(R25),
    .in26(R26), .in27(R27), .in28(R28), .in29(R29), .in30(R30), .out(Data_B), .sel(SB));  // open: in31

  assign LH_RW_2 = LH_RW;

  // Other names for the same wires on the sheet: Hi_t[31:0] = Hi_2; Lo_t[31:0] = Lo_2; LoHiRW = LH_RW; Rst = Reset;
  //   SP_IN[31:0] = SP; SP_t[31:0] = Stack_Pointer

  // Notes on the sheet:
  //   Inputs
  //   Data Address
  //   Data In
  //   Read/Write
  //   Selector A
  //   Selector B
  //   Lo HIi R/W
  //   Lo
  //   Hi
  //   SP R/W
  //   SP
  //   Outputs
endmodule

module Register_32_bits (
  input  [31:0] Data_In,
  input  Load,
  input  Clock,
  input  Reset,
  output [31:0] Current_Value
);

  Register #(.width(32), .trigger("falling")) register_1 (
    .D(Data_In), .en(Load), .Q(Current_Value), .clk(Clock), .clr(Reset));
  // Probe on Current_Value

  // Notes on the sheet:
  //   Register 32 bits
endmodule

module Test_Register_File (
  input  [4:0] in_1,
  input  [4:0] in_2,
  input  [31:0] in_3,
  input  [4:0] in_4,
  input  in_5,
  input  in_6,
  output [31:0] out_7,
  output [31:0] out_8
);

  wire register_file_32x32_bits_1_p6;

  // Probe on in_3
  // Register_File_32x32_bits register_file_32x32_bits_1: pin names not known; wires that end beside it: in_1, in_2, in_3, in_4, in_5, register_file_32x32_bits_1_p6
  Clock clock_1 (.out(register_file_32x32_bits_1_p6));
  // Probe on out_7
  // Probe on out_8
endmodule

module ALU_2 (
  input  [31:0] A,
  input  [31:0] B,
  input  [2:0] S,
  output [31:0] R,
  output Positive,
  output Zero,
  output Negative,
  output [31:0] Lo,
  output [31:0] Hi
);

  wire comparator_1_lt, comparator_2_lt;
  wire [31:0] And, Diff, HiDiv, HiDivu, HiMult, HiMulu, LoDiv, LoDivu, LoMult, LoMulu, Nor, Or, slt, sltu,
       Sum, Xor;

  // Probe on A
  // Probe on B
  Adder #(.width(32)) adder_1 (.a(A), .b(B), .out(Sum));  // open: cin, cout
  Subtractor #(.width(32)) subtractor_1 (.a(A), .b(B), .out(Diff));  // open: bin, bout
  assign And = A & B;  // AND_Gate and_1, 32 bits wide
  assign Or = A | B;  // OR_Gate or_1, 32 bits wide
  assign Nor = ~Or;  // NOT_Gate not_1, 32 bits wide
  assign Xor = A ^ B;  // XOR_Gate xor_1, 32 bits wide
  Signed_MUltiplier signed_multiplier_1 (.A(A), .B(B), .Low(LoMult), .High(HiMult));
  Multiplier #(.width(32)) multiplier_1 (.a(A), .b(B), .out(LoMulu), .cout(HiMulu));  // open: cin
  Comparator #(.width(32)) comparator_1 (.a(A), .b(B), .lt(comparator_1_lt));  // open: gt, eq
  Comparator #(.width(32), .mode("unsigned")) comparator_2 (.a(A), .b(B), .lt(comparator_2_lt));  // open: gt, eq
  Signed_Div signed_div_1 (.A(A), .B(B), .Low(LoDiv), .High(HiDiv));
  Divider #(.width(32)) divider_1 (.a(A), .b(B), .out(LoDivu), .rem(HiDivu));  // open: upper
  assign slt = {{31{1'b0}}, comparator_1_lt};  // Bit_Extender bit_extender_1
  assign sltu = {{31{1'b0}}, comparator_2_lt};  // Bit_Extender bit_extender_2
  Multiplexer #(.select(3), .width(32), .enable("false")) multiplexer_1 (
    .in0(Sum), .in1(Diff), .in2(And), .in3(Or), .in4(Nor), .in6(Xor), .out(R), .sel(S));  // open: in5, in7
  Multiplexer #(.select(2), .width(32), .enable("false")) multiplexer_2 (
    .in0(LoMult), .in1(LoMulu), .in2(LoDiv), .in3(LoDivu), .out(Lo), .sel(S[1:0]));
  Multiplexer #(.select(2), .width(32), .enable("false")) multiplexer_3 (
    .in0(HiMult), .in1(HiMulu), .in2(HiDiv), .in3(HiDivu), .out(Hi), .sel(S[1:0]));
  Comparator #(.width(32)) comparator_3 (.a(R), .b({32{1'b0}}), .gt(Positive), .eq(Zero), .lt(Negative));

  // Other names for the same wires on the sheet: LoHi_S[1:0] = S[1:0]

  // Notes on the sheet:
  //   Inputs
  //   ALU
  //   Arithmetic Ops
  //   Logic Ops
  //   Unisgned
  //   Outputs
endmodule

module Test_ALU (
  input  [31:0] B,
  input  in_2,
  input  [31:0] B_2,
  input  [3:0] in_4,
  input  in_5,
  output out_6,
  output out_7,
  output [31:0] out_8
);

  wire alu_1_p6;
  wire [31:0] multiplexer_1_out, multiplexer_2_out, negator_1_out, negator_2_out;

  Negator #(.width(32)) negator_1 (.in(B), .out(negator_1_out));
  Negator #(.width(32)) negator_2 (.in(B_2), .out(negator_2_out));
  Multiplexer #(.width(32), .enable("false")) multiplexer_1 (
    .in0(B), .in1(negator_1_out), .out(multiplexer_1_out), .sel(in_2));
  Multiplexer #(.width(32), .enable("false")) multiplexer_2 (
    .in0(B_2), .in1(negator_2_out), .out(multiplexer_2_out), .sel(in_5));
  // Probe on multiplexer_1_out
  // Probe on multiplexer_2_out
  // ALU_2 alu_1: pin names not known; wires that end beside it: multiplexer_1_out, multiplexer_2_out, in_4, out_7, out_6, alu_1_p6, out_8
  // Probe on out_8
  // Probe on alu_1_p6
  // Probe on alu_1_p6

  // Notes on the sheet:
  //   ALU Tester
  //   Unsigned
endmodule

module Signed_MUltiplier (
  input  [31:0] A,
  input  [31:0] B,
  output [31:0] Low,
  output [31:0] High
);

  wire adder_1_cout, Sign_A, Sign_B, Sign_R;
  wire [31:0] abs_1_out, abs_2_out, minus_High, minus_Low, not_1_out, not_2_out, plus_High, plus_Low;

  // Probe on A
  // Probe on B
  ABS abs_1 (.In(A), .Out(abs_1_out), .Sign(Sign_A));
  ABS abs_2 (.In(B), .Out(abs_2_out), .Sign(Sign_B));
  xor xor_1 (Sign_R, Sign_A, Sign_B);
  Multiplier #(.width(32)) multiplier_1 (.a(abs_1_out), .b(abs_2_out), .out(plus_Low), .cout(plus_High));  // open: cin
  assign not_1_out = ~plus_Low;  // NOT_Gate not_1, 32 bits wide
  assign not_2_out = ~plus_High;  // NOT_Gate not_2, 32 bits wide
  Adder #(.width(32)) adder_1 (.a(not_1_out), .b(32'h1), .out(minus_Low), .cout(adder_1_cout));  // open: cin
  Adder #(.width(32)) adder_2 (.a(not_2_out), .b({32{1'b0}}), .out(minus_High), .cin(adder_1_cout));  // open: cout
  // Probe on Low
  Multiplexer #(.width(32), .enable("false")) multiplexer_1 (.in0(plus_Low), .in1(minus_Low), .out(Low), .sel(Sign_R));
  Multiplexer #(.width(32), .enable("false")) multiplexer_2 (
    .in0(plus_High), .in1(minus_High), .out(High), .sel(Sign_R));
  // Probe on High

  // Notes on the sheet:
  //   Final Sign
  //   Signed Multiplier
  //   Negator
  //   1) Multiply the operand's absolute value
  //   2) Invert the result if neccesary according to the signs of the operands
  //   Outputs
endmodule

module Signed_Div (
  input  [31:0] A,
  input  [31:0] B,
  output [31:0] Low,
  output [31:0] High
);

  wire Sign_A, Sign_B, Sign_Quo;
  wire [31:0] abs_1_out, abs_2_out, minus_Quo, minus_Rem, plus_Quo, plus_Rem;

  // Probe on A
  // Probe on B
  ABS abs_1 (.In(A), .Out(abs_1_out), .Sign(Sign_A));
  ABS abs_2 (.In(B), .Out(abs_2_out), .Sign(Sign_B));
  xor xor_1 (Sign_Quo, Sign_A, Sign_B);
  Divider #(.width(32)) divider_1 (.a(abs_1_out), .b(abs_2_out), .out(plus_Quo), .rem(plus_Rem));  // open: upper
  Negator #(.width(32)) negator_1 (.in(plus_Quo), .out(minus_Quo));
  Negator #(.width(32)) negator_2 (.in(plus_Rem), .out(minus_Rem));
  // Probe on Low
  Multiplexer #(.width(32), .enable("false")) multiplexer_1 (
    .in0(plus_Quo), .in1(minus_Quo), .out(Low), .sel(Sign_Quo));
  Multiplexer #(.width(32), .enable("false")) multiplexer_2 (.in0(plus_Rem), .in1(minus_Rem), .out(High), .sel(Sign_A));
  // Probe on High

  // Notes on the sheet:
  //   Signed Divider
  //   Quotient Sign
  //   Negator
  //   1) Divide the operand's absolute value
  //   2) Negate the quotient if the signs of the operands are opposite
  //   3) Make the sign of the remainder match the dividend
  //   Outputs
endmodule

module ABS (
  input  [31:0] In,
  output [31:0] Out,
  output Sign
);

  wire [31:0] negator_1_out;

  BitSelector #(.width(32)) bitselector_1 (.in(In), .out(Sign), .sel({5{1'b1}}));
  Multiplexer #(.width(32), .enable("false")) multiplexer_1 (.in0(In), .in1(negator_1_out), .out(Out), .sel(Sign));
  Negator #(.width(32)) negator_1 (.in(In), .out(negator_1_out));

  // Notes on the sheet:
  //   Absolute Value and Sign
endmodule

module Instruction_Decoder (
  input  [31:0] Inst,
  input  IM_R_W,
  input  Clk,
  input  Rst,
  output [5:0] Op,
  output [5:0] Func__Code,
  output [25:0] Destino,
  output [4:0] RS,
  output [4:0] RT,
  output [4:0] RD,
  output [31:0] Sign_Const,
  output [31:0] Unsgn_Const
);

  // Probe on {Op, Destino}
  Register_32_bits Instruction_Memory (
    .Data_In(Inst), .Clock(Clk), .Reset(Rst), .Current_Value({Op, Destino}), .Load(IM_R_W));
  assign Sign_Const = {{16{Destino[15]}}, Destino[15:0]};  // Bit_Extender bit_extender_1
  assign Unsgn_Const = {{16{1'b0}}, Destino[15:0]};  // Bit_Extender bit_extender_2

  assign Func__Code = Destino[5:0];
  assign RD = Destino[15:11];
  assign RS = Destino[25:21];
  assign RT = Destino[20:16];

  // Other names for the same wires on the sheet: Destin[25:0] = Destino; FC[5:0] = Destino[5:0];
  //   K[15:0] = Destino[15:0]

  // Notes on the sheet:
  //   Inputs
  //   Outputs
endmodule

module DataPath (
  input  [31:0] RAM_out,
  input  DAS,
  input  DOS,
  input  AS,
  input  [1:0] BS,
  input  [1:0] BCS,
  input  [1:0] AddrS,
  input  [2:0] DIS,
  input  [2:0] ALUS,
  input  [2:0] FlagS,
  input  IM_R_W,
  input  PC_R_W,
  input  LH_R_W,
  input  RF_R_W,
  input  [6:0] KBD_Data,
  input  SP_R_W,
  input  KBD_Avail,
  input  Clk,
  input  RST,
  output [31:0] Address,
  output [31:0] Data_Out,
  output [5:0] OpCode,
  output [5:0] FuncCode,
  output [6:0] tty_out
);

  wire N, P, Z;
  wire [4:0] DA, RD, RS, RT;
  wire [25:0] Dest;
  wire [31:0] bit_extender_1_out, branch_control_1_pc_out, Hi, HiI, K, kbd, Lo, LoI, multiplexer_1_out,
       multiplexer_4_out, multiplexer_5_out, PC, R, rnd, RT_t, SP, UK;
  wire [31:7] RS_t;

  Instruction_Decoder instruction_decoder_1 (
    .Inst(RAM_out), .IM_R_W(IM_R_W), .Clk(Clk), .Func__Code(FuncCode), .RS(RS), .RT(RT), .Destino(Dest),
    .Sign_Const(K), .Op(OpCode), .Unsgn_Const(UK), .RD(RD), .Rst(RST));
  Multiplexer #(.select(3), .width(32), .enable("false")) multiplexer_1 (
    .in0(R), .in1(RAM_out), .in2(Lo), .in4(Hi), .in6(rnd), .in7(kbd), .out(multiplexer_1_out), .sel(DIS));  // open: in3, in5
  Multiplexer #(.width(5), .enable("false")) multiplexer_2 (.in0(RD), .in1(RT), .out(DA), .sel(DAS));
  assign bit_extender_1_out = {{25{1'b0}}, KBD_Data};  // Bit_Extender bit_extender_1
  Register_File_32x32_bits register_file_32x32_bits_1 (
    .DA(DA), .DI(multiplexer_1_out), .R_W(RF_R_W), .SA(RS), .SB(RT), .Clk(Clk), .Reset(RST),
    .Data_A({RS_t, tty_out}), .Data_B(RT_t), .Lo(LoI), .LH_RW(LH_R_W), .Hi(HiI), .Lo_2(Lo), .Hi_2(Hi),
    .Stack_Pointer(SP), .SP(R), .LH_RW_2(SP_R_W));
  Multiplexer #(.width(32), .enable("false")) multiplexer_3 (
    .in0(bit_extender_1_out), .in1({32{1'b1}}), .out(kbd), .sel(KBD_Avail));
  Branch_Control_2 branch_control_1 (
    .PC_in(PC), .K(K), .PC_out(branch_control_1_pc_out), .Destino(Dest), .Register({RS_t, tty_out}),
    .BCSel(BCS), .P(P), .Z(Z), .N(N), .FlagS(FlagS));
  Multiplexer #(.width(32), .enable("false")) multiplexer_4 (
    .in0({RS_t, tty_out}), .in1(SP), .out(multiplexer_4_out), .sel(AS));
  Multiplexer #(.select(2), .width(32), .enable("false")) multiplexer_5 (
    .in0(RT_t), .in1(K), .in2(UK), .in3(32'h4), .out(multiplexer_5_out), .sel(BS));
  Random #(.width(32)) random_1 (.clk(Clk), .out(rnd));  // open: next, clr
  Register_32_bits register_32_bits_1 (
    .Data_In(branch_control_1_pc_out), .Clock(Clk), .Reset(RST), .Current_Value(PC), .Load(PC_R_W));
  ALU_2 alu_1 (
    .A(multiplexer_4_out), .B(multiplexer_5_out), .S(ALUS), .Zero(Z), .Negative(N), .R(R), .Hi(HiI),
    .Lo(LoI), .Positive(P));
  Multiplexer #(.select(2), .width(32), .enable("false")) multiplexer_6 (
    .in0(PC), .in1(R), .in2(SP), .out(Address), .sel(AddrS));  // open: in3
  Multiplexer #(.width(32), .enable("false")) multiplexer_7 (
    .in0(RT_t), .in1({RS_t, tty_out}), .out(Data_Out), .sel(DOS));
  // Probe on RS
  // Probe on RT
  // Probe on RD
  // Probe on DA
  // Probe on K
  // Probe on UK
  // Probe on Dest
  // Probe on R
  // Probe on PC

  // Other names for the same wires on the sheet: Func[5:0] = FuncCode; IM_RW = IM_R_W; LH_RW = LH_R_W;
  //   OP[5:0] = OpCode; PC_RW = PC_R_W; RAM[31:0] = RAM_out; RF_RW = RF_R_W; RS_t[6:0] = tty_out; SP_RW = SP_R_W

  // Notes on the sheet:
  //   Selectors
  //   Loads
  //   Data Path
  //   PC
  //   DEBUG
endmodule

module Branch_Control_2 (
  input  [31:0] PC_in,
  input  [1:0] BCSel,
  input  [2:0] FlagS,
  input  [31:0] K,
  input  [25:0] Destino,
  input  [31:0] Register,
  input  Z,
  input  N,
  input  P,
  output [31:0] PC_out
);

  wire Flag, lez, neq;
  wire [31:0] adder_1_out, adder_2_out, multiplexer_2_out, shifter_1_out;

  not not_1 (neq, Z);
  Multiplexer #(.select(3), .enable("false")) multiplexer_1 (
    .in0(Z), .in2(lez), .in4(neq), .in6(N), .in7(P), .out(Flag), .sel(FlagS));  // open: in1, in3, in5
  not not_2 (lez, P);
  Adder #(.width(32)) adder_1 (.a(PC_in), .b(32'h4), .out(adder_1_out));  // open: cin, cout
  Shifter #(.width(32)) shifter_1 (.in(K), .\dist (5'b00010), .out(shifter_1_out));
  Adder #(.width(32)) adder_2 (.a(adder_1_out), .b(shifter_1_out), .out(adder_2_out));  // open: cin, cout
  Multiplexer #(.width(32), .enable("false")) multiplexer_2 (
    .in0(adder_1_out), .in1(adder_2_out), .out(multiplexer_2_out), .sel(Flag));
  Multiplexer #(.select(2), .width(32), .enable("false")) multiplexer_3 (
    .in0(adder_1_out), .in1(multiplexer_2_out), .in2(Register), .in3({PC_in[31:28], Destino, 2'b00}),
    .out(PC_out), .sel(BCSel));

  // Other names for the same wires on the sheet: BCS[1:0] = BCSel; eq = Z; FS[2:0] = FlagS; gtz = P; ltz = N;
  //   R[31:0] = Register

  // Notes on the sheet:
  //   Direccion de la
  //   Instruccion Actual
  //   Branch Control
  //   Direccion de la
  //   Proxima Instruccion
endmodule

module Test_Branch_Control (
  input  [31:0] in_1,
  input  in_2,
  input  in_3,
  input  [15:0] in_4,
  output [31:0] out_5
);

  // Probe on in_1
  // Probe on in_4
  Branch_Control_2 branch_control_1 (.PC_out(out_5));  // open: PC_in, K, Destino, Register, BCSel, P, Z, N, FlagS
  // Probe on out_5
endmodule
